# Fritzing sketch UB_compact (saved by Fritzing 0.9.3b)
breadboards: 1

parts:
  Composant1 = Arduino Nano (Rev3.0)
  R1 = Resistor [tolerance=±10% resistance=100 package=THT]
  Q1 = NPN-Transistor [part_number=BC547 package="TO92 [THT]"]
  S1 = Taiway 100-SP-X-T1 SPDT Miniature Toggle Switch [part_number=100-SP-X-T1-0-0-B1-M1 package=THT]
  J1 = Basic Servo

nets:
  N1: Composant1.GND, Q1.E, S1.COM
  N2: Composant1.D2, R1.Pin_1
  N3: Composant1.D3, J1.pulse
  N4: Composant1.D8, S1.L1
  5V: Composant1.5V, J1.vcc
  N5: R1.Pin_0, Q1.B
  N6: Q1.C, J1.gnd
